# Fritzing sketch ad8232 (saved by Fritzing 0.9.3b)
breadboards: 1

parts:
  Mod1 = AD8232 HeartRate Monitor [part_number=SEN-12650]
  U1 = ESP32-38PinWide [part_number=ESP32-38PinWide]

nets:
  GND: Mod1.GND, U1.GND
  N1: Mod1.3.3v, U1.3.3
  N2: Mod1.OUTPUT, U1.GPIO34
  N3: Mod1.LO-, U1.GPIO18
  N4: Mod1.LO+, U1.GPIO19

custom parts:
  AD8232 HeartRate Monitor: Sparkfun single lead heart rate monitor - Ad8232.
  ESP32-38PinWide: Generic 38-Pin ESP32 with wide format (only access to one side of pins on a breadboard) based on Stephen Lilley's HiLetgo ESP-WROOM-32 ESP32 ESP-32S Development Board.
