# Fritzing sketch emg (saved by Fritzing 0.9.3b)
breadboards: 1

parts:
  M1 = advancer muscle sensor v3
  LLC1 = Logic Level Converter [package="Breakout board"]
  VCC1 = 4 x AAA Battery Mount
  U1 = ESP32-38PinWide [part_number=ESP32-38PinWide]

nets:
  N1: M1.+Vs, LLC1.HV, VCC1.+
  N2: M1.GND, LLC1.H-GND, VCC1.-
  N3: M1.SIG, LLC1.HV1
  N4: LLC1.LV1, U1.GPIO35
  N5: LLC1.LV, U1.3.3
  N6: LLC1.L-GND, U1.GND

custom parts:
  advancer muscle sensor v3: This sensor will measure the filtered and rectified electrical activity of a muscle; outputting 0-Vs Volts depending the amount of activity in the selected muscle, where Vs signifies the voltage of the power source. Power supply voltage: min. +-3.5V.
  Logic Level Converter: 5V to/from 3.3V logic level converter
  ESP32-38PinWide: Generic 38-Pin ESP32 with wide format (only access to one side of pins on a breadboard) based on Stephen Lilley's HiLetgo ESP-WROOM-32 ESP32 ESP-32S Development Board.
