# Fritzing sketch heartrate (saved by Fritzing 0.9.3b)
breadboards: 1

parts:
  M1 = MAX30102
  U1 = ESP32-38PinWide [part_number=ESP32-38PinWide]

nets:
  N1: M1.VIN, U1.3.3
  N2: M1.SCL, U1.GPIO22
  N3: M1.SDA, U1.GPIO21
  GND: M1.GND, U1.GND

custom parts:
  MAX30102: Oximeter module using the MAX30102 chip. You may wish to read (and check your module) this post on power problems with these modules: https://reedpaper.wordpress.com/2018/08/22/pulse-oximeter-max30100-max30102-how-to-fix-wrong-board/ . As usual, if you want the mounting holes in pcb, you need to drag a hole over the pad in silkscreen to actually drill the hole (by default they are not drilled)
  ESP32-38PinWide: Generic 38-Pin ESP32 with wide format (only access to one side of pins on a breadboard) based on Stephen Lilley's HiLetgo ESP-WROOM-32 ESP32 ESP-32S Development Board.
