# Fritzing sketch pantallalcd (saved by Fritzing 0.9.3b)
breadboards: 1

parts:
  LCM1602_IIC1 = LCM1602 IIC [part_number="LCM1602 IIC" chip_label="LCM1602 IIC" package="DIP (Dual Inline) [THT]"]
  LCD1 = LCD screen
  LLC1 = Logic Level Converter [package="Breakout board"]
  VCC1 = 4 x AAA Battery Mount
  U1 = ESP32-38PinWide [part_number=ESP32-38PinWide]

nets:
  VSS: LCM1602_IIC1.VSS, LCD1.VSS
  VDD: LCM1602_IIC1.VDD, LCD1.VDD
  N1: LCM1602_IIC1.V0, LCD1.V0
  N2: LCM1602_IIC1.RS, LCD1.RS
  N3: LCM1602_IIC1.RW, LCD1.R/W
  N4: LCM1602_IIC1.E, LCD1.E
  N5: LCM1602_IIC1.D0, LCD1.DB0
  N6: LCM1602_IIC1.D1, LCD1.DB1
  N7: LCM1602_IIC1.D2, LCD1.DB2
  N8: LCM1602_IIC1.D3, LCD1.DB3
  N9: LCM1602_IIC1.D4, LCD1.DB4
  N10: LCM1602_IIC1.D5, LCD1.DB5
  N11: LCM1602_IIC1.D6, LCD1.DB6
  N12: LCM1602_IIC1.D7, LCD1.DB7
  N13: LCM1602_IIC1.A, LCD1.LED+
  N14: LCM1602_IIC1.K, LCD1.LED-
  N15: LCM1602_IIC1.GND, LLC1.H-GND, VCC1.-
  N16: LCM1602_IIC1.VCC, LLC1.HV, VCC1.+
  N17: LCM1602_IIC1.SDA, LLC1.HV3
  N18: LCM1602_IIC1.SCL, LLC1.HV1
  N19: LLC1.LV1, U1.GPIO22
  N20: LLC1.LV, U1.3.3
  N21: LLC1.L-GND, U1.GND
  N22: LLC1.LV4, U1.GPIO21

custom parts:
  LCM1602 IIC: I2C-Module to use a 1602 or 2004 LCD on with the wire.h libory Serial LCD Modul
  Logic Level Converter: 5V to/from 3.3V logic level converter
  ESP32-38PinWide: Generic 38-Pin ESP32 with wide format (only access to one side of pins on a breadboard) based on Stephen Lilley's HiLetgo ESP-WROOM-32 ESP32 ESP-32S Development Board.
