# Fritzing sketch teclado (saved by Fritzing 0.9.3b)
breadboards: 1

parts:
  Keypad4x1 = Keypad Membran 4x4
  U1 = ESP32-38PinWide [part_number=ESP32-38PinWide]

nets:
  N1: Keypad4x1.Pin1, U1.GPIO15
  N2: Keypad4x1.Pin2, U1.GPIO14
  N3: Keypad4x1.Pin3, U1.GPIO13
  N4: Keypad4x1.Pin4, U1.GPIO27
  N5: Keypad4x1.Pin5, U1.GPIO26
  N6: Keypad4x1.Pin6, U1.GPIO25
  N7: Keypad4x1.Pin7, U1.GPIO33
  N8: Keypad4x1.Pin8, U1.GPIO32

custom parts:
  Keypad Membran 4x4: Membrane Keypad 4x4 Matrix
  ESP32-38PinWide: Generic 38-Pin ESP32 with wide format (only access to one side of pins on a breadboard) based on Stephen Lilley's HiLetgo ESP-WROOM-32 ESP32 ESP-32S Development Board.
