# Fritzing sketch tfg (saved by Fritzing 0.9.3b)
breadboards: 1

parts:
  U1 = ESP32-38PinWide [part_number=ESP32-38PinWide]
  Keypad4x1 = Keypad Membran 4x4
  Mod1 = AD8232 HeartRate Monitor [part_number=SEN-12650]
  LLC1 = Logic Level Converter [package="Breakout board"]
  M1 = MAX30102
  LCM1602_IIC1 = LCM1602 IIC [part_number="LCM1602 IIC" chip_label="LCM1602 IIC" package="DIP (Dual Inline) [THT]"]
  LCD1 = LCD screen
  M2 = advancer muscle sensor v3
  VCC1 = 4 x AAA Battery Mount

nets:
  3.3V: U1.3.3, Mod1.3.3v, LLC1.LV, M1.VIN
  N1: U1.GPIO34, Mod1.OUTPUT
  N2: U1.GPIO35, LLC1.LV4
  N3: U1.GPIO32, Keypad4x1.Pin8
  N4: U1.GPIO33, Keypad4x1.Pin7
  N5: U1.GPIO25, Keypad4x1.Pin6
  N6: U1.GPIO26, Keypad4x1.Pin5
  N7: U1.GPIO27, Keypad4x1.Pin4
  N8: U1.GPIO14, Keypad4x1.Pin2
  N9: U1.GPIO13, Keypad4x1.Pin3
  N10: U1.GPIO15, Keypad4x1.Pin1
  N11: U1.GPIO18, Mod1.LO-
  N12: U1.GPIO19, Mod1.LO+
  N13: U1.GPIO21, LLC1.LV2, M1.SDA
  N14: U1.GPIO22, LLC1.LV3, M1.SCL
  GND: U1.GND, Mod1.GND, LLC1.L-GND, M1.GND
  N15: LLC1.HV4, M2.SIG
  N16: LLC1.HV3, LCM1602_IIC1.SCL
  GND_2: LLC1.H-GND, LCM1602_IIC1.GND, M2.GND, VCC1.-
  N17: LLC1.HV, LCM1602_IIC1.VCC, M2.+Vs, VCC1.+
  N18: LLC1.HV2, LCM1602_IIC1.SDA
  VSS: LCM1602_IIC1.VSS, LCD1.VSS
  VDD: LCM1602_IIC1.VDD, LCD1.VDD
  N19: LCM1602_IIC1.V0, LCD1.V0
  N20: LCM1602_IIC1.RS, LCD1.RS
  N21: LCM1602_IIC1.RW, LCD1.R/W
  N22: LCM1602_IIC1.E, LCD1.E
  N23: LCM1602_IIC1.D0, LCD1.DB0
  N24: LCM1602_IIC1.D1, LCD1.DB1
  N25: LCM1602_IIC1.D2, LCD1.DB2
  N26: LCM1602_IIC1.D3, LCD1.DB3
  N27: LCM1602_IIC1.D4, LCD1.DB4
  N28: LCM1602_IIC1.D5, LCD1.DB5
  N29: LCM1602_IIC1.D6, LCD1.DB6
  N30: LCM1602_IIC1.D7, LCD1.DB7
  N31: LCM1602_IIC1.A, LCD1.LED+
  N32: LCM1602_IIC1.K, LCD1.LED-

custom parts:
  ESP32-38PinWide: Generic 38-Pin ESP32 with wide format (only access to one side of pins on a breadboard) based on Stephen Lilley's HiLetgo ESP-WROOM-32 ESP32 ESP-32S Development Board.
  Keypad Membran 4x4: Membrane Keypad 4x4 Matrix
  AD8232 HeartRate Monitor: Sparkfun single lead heart rate monitor - Ad8232.
  Logic Level Converter: 5V to/from 3.3V logic level converter
  MAX30102: Oximeter module using the MAX30102 chip. You may wish to read (and check your module) this post on power problems with these modules: https://reedpaper.wordpress.com/2018/08/22/pulse-oximeter-max30100-max30102-how-to-fix-wrong-board/ . As usual, if you want the mounting holes in pcb, you need to drag a hole over the pad in silkscreen to actually drill the hole (by default they are not drilled)
  LCM1602 IIC: I2C-Module to use a 1602 or 2004 LCD on with the wire.h libory Serial LCD Modul
  advancer muscle sensor v3: This sensor will measure the filtered and rectified electrical activity of a muscle; outputting 0-Vs Volts depending the amount of activity in the selected muscle, where Vs signifies the voltage of the power source. Power supply voltage: min. +-3.5V.
